// Logisim project cpu.circ as structural Verilog: 8 circuits, main circuit main
module main (
);

  RegisterFile registerfile_1 ();  // open: read02, read01, datain, clk, WriteEnable, dataout1, reset, dataout2, writereg
  DRAM dram_1 ();  // open: dataOut, DMwe, addrIn, clk, dataIn
endmodule

module RegisterFile (
  input  reset,
  input  clk,
  input  WriteEnable,
  input  [2:0] read01,
  input  [15:0] datain,
  input  [2:0] writereg,
  input  [2:0] read02,
  output [15:0] dataout1,
  output [15:0] dataout2
);

  wire clk_t, decoder_1_out1, decoder_1_out2, decoder_1_out3, decoder_1_out4, decoder_1_out5, decoder_1_out6,
       decoder_1_out7, r10, r11, r12, r13, r14, r15, r16, r17, r20, r21, r22, r23, r24, r25, r26, r27;
  wire [15:0] reg0_dataout, reg1_dataout, reg2_dataout, reg3_dataout, reg4_dataout, reg5_dataout,
       reg6_dataout, reg7_dataout;

  and and_1 (clk_t, clk, WriteEnable);
  Decoder #(.select(3), .enable("false")) decoder_1 (
    .out1(decoder_1_out1), .out2(decoder_1_out2), .out3(decoder_1_out3), .out4(decoder_1_out4),
    .out5(decoder_1_out5), .out6(decoder_1_out6), .out7(decoder_1_out7), .sel(writereg));  // open: out0
  // Probe on reg7_dataout
  SingleReg reg7 (.clk(clk_t), .reset(reset), .WrtEn(decoder_1_out7), .datain(datain), .dataout(reg7_dataout));
  // Probe on reg6_dataout
  SingleReg reg6 (.clk(clk_t), .reset(reset), .WrtEn(decoder_1_out6), .datain(datain), .dataout(reg6_dataout));
  // Probe on reg5_dataout
  SingleReg reg5 (.clk(clk_t), .reset(reset), .WrtEn(decoder_1_out5), .datain(datain), .dataout(reg5_dataout));
  // Probe on reg4_dataout
  SingleReg reg4 (.clk(clk_t), .reset(reset), .WrtEn(decoder_1_out4), .datain(datain), .dataout(reg4_dataout));
  // Probe on reg3_dataout
  SingleReg reg3 (.clk(clk_t), .reset(reset), .WrtEn(decoder_1_out3), .datain(datain), .dataout(reg3_dataout));
  // Probe on reg2_dataout
  SingleReg reg2 (.clk(clk_t), .reset(reset), .WrtEn(decoder_1_out2), .datain(datain), .dataout(reg2_dataout));
  // Probe on reg1_dataout
  SingleReg reg1 (.clk(clk_t), .reset(reset), .WrtEn(decoder_1_out1), .datain(datain), .dataout(reg1_dataout));
  // Probe on reg0_dataout
  SingleReg reg0 (.clk(clk_t), .reset(reset), .WrtEn(1'b0), .datain({16{1'b0}}), .dataout(reg0_dataout));
  assign dataout1 = r17 ? reg7_dataout : 16'bz;  // Controlled_Buffer controlled_buffer_1
  assign dataout1 = r16 ? reg6_dataout : 16'bz;  // Controlled_Buffer controlled_buffer_2
  assign dataout1 = r15 ? reg5_dataout : 16'bz;  // Controlled_Buffer controlled_buffer_3
  assign dataout1 = r14 ? reg4_dataout : 16'bz;  // Controlled_Buffer controlled_buffer_4
  assign dataout1 = r13 ? reg3_dataout : 16'bz;  // Controlled_Buffer controlled_buffer_5
  assign dataout1 = r12 ? reg2_dataout : 16'bz;  // Controlled_Buffer controlled_buffer_6
  assign dataout1 = r11 ? reg1_dataout : 16'bz;  // Controlled_Buffer controlled_buffer_7
  assign dataout1 = r10 ? reg0_dataout : 16'bz;  // Controlled_Buffer controlled_buffer_8
  assign dataout2 = r27 ? reg7_dataout : 16'bz;  // Controlled_Buffer controlled_buffer_9
  assign dataout2 = r26 ? reg6_dataout : 16'bz;  // Controlled_Buffer controlled_buffer_10
  assign dataout2 = r25 ? reg5_dataout : 16'bz;  // Controlled_Buffer controlled_buffer_11
  assign dataout2 = r24 ? reg4_dataout : 16'bz;  // Controlled_Buffer controlled_buffer_12
  assign dataout2 = r23 ? reg3_dataout : 16'bz;  // Controlled_Buffer controlled_buffer_13
  assign dataout2 = r22 ? reg2_dataout : 16'bz;  // Controlled_Buffer controlled_buffer_14
  assign dataout2 = r21 ? reg1_dataout : 16'bz;  // Controlled_Buffer controlled_buffer_15
  assign dataout2 = r20 ? reg0_dataout : 16'bz;  // Controlled_Buffer controlled_buffer_16
  Decoder #(.select(3), .enable("false")) decoder_2 (
    .out0(r10), .out1(r11), .out2(r12), .out3(r13), .out4(r14), .out5(r15), .out6(r16), .out7(r17),
    .sel(read01));
  Decoder #(.select(3), .enable("false")) decoder_3 (
    .out0(r20), .out1(r21), .out2(r22), .out3(r23), .out4(r24), .out5(r25), .out6(r26), .out7(r27),
    .sel(read02));

  // Other names for the same wires on the sheet: R = reset
endmodule

module SingleReg (
  input  clk,
  input  reset,
  input  WrtEn,
  input  [15:0] datain,
  output [15:0] dataout
);

  wire clkin;

  and and_1 (clkin, clk, WrtEn);
  D_Flip_Flop d_ff_1 (.D(datain[15]), .clk(clkin), .Q(dataout[15]), .reset(reset));  // open: Qn, preset
  D_Flip_Flop d_ff_2 (.D(datain[13]), .clk(clkin), .Q(dataout[13]), .reset(reset));  // open: Qn, preset
  D_Flip_Flop d_ff_3 (.D(datain[11]), .clk(clkin), .Q(dataout[11]), .reset(reset));  // open: Qn, preset
  D_Flip_Flop d_ff_4 (.D(datain[9]), .clk(clkin), .Q(dataout[9]), .reset(reset));  // open: Qn, preset
  D_Flip_Flop d_ff_5 (.D(datain[7]), .clk(clkin), .Q(dataout[7]), .reset(reset));  // open: Qn, preset
  D_Flip_Flop d_ff_6 (.D(datain[5]), .clk(clkin), .Q(dataout[5]), .reset(reset));  // open: Qn, preset
  D_Flip_Flop d_ff_7 (.D(datain[3]), .clk(clkin), .Q(dataout[3]), .reset(reset));  // open: Qn, preset
  D_Flip_Flop d_ff_8 (.D(datain[1]), .clk(clkin), .Q(dataout[1]), .reset(reset));  // open: Qn, preset
  D_Flip_Flop d_ff_9 (.D(datain[14]), .clk(clkin), .Q(dataout[14]), .reset(reset));  // open: Qn, preset
  D_Flip_Flop d_ff_10 (.D(datain[12]), .clk(clkin), .Q(dataout[12]), .reset(reset));  // open: Qn, preset
  D_Flip_Flop d_ff_11 (.D(datain[10]), .clk(clkin), .Q(dataout[10]), .reset(reset));  // open: Qn, preset
  D_Flip_Flop d_ff_12 (.D(datain[8]), .clk(clkin), .Q(dataout[8]), .reset(reset));  // open: Qn, preset
  D_Flip_Flop d_ff_13 (.D(datain[6]), .clk(clkin), .Q(dataout[6]), .reset(reset));  // open: Qn, preset
  D_Flip_Flop d_ff_14 (.D(datain[4]), .clk(clkin), .Q(dataout[4]), .reset(reset));  // open: Qn, preset
  D_Flip_Flop d_ff_15 (.D(datain[2]), .clk(clkin), .Q(dataout[2]), .reset(reset));  // open: Qn, preset
  D_Flip_Flop d_ff_16 (.D(datain[0]), .clk(clkin), .Q(dataout[0]), .reset(reset));  // open: Qn, preset

  // Other names for the same wires on the sheet: b0 = datain[0]; b1 = datain[1]; b2 = datain[2]; b3 = datain[3];
  //   b4 = datain[4]; b5 = datain[5]; b6 = datain[6]; b7 = datain[7]; b8 = datain[8]; b9 = datain[9];
  //   b10 = datain[10]; b11 = datain[11]; b12 = datain[12]; b13 = datain[13]; b14 = datain[14]; b15 = datain[15];
  //   o0 = dataout[0]; o1 = dataout[1]; o2 = dataout[2]; o3 = dataout[3]; o4 = dataout[4]; o5 = dataout[5];
  //   o6 = dataout[6]; o7 = dataout[7]; o8 = dataout[8]; o9 = dataout[9]; o10 = dataout[10]; o11 = dataout[11];
  //   o12 = dataout[12]; o13 = dataout[13]; o14 = dataout[14]; o15 = dataout[15]
endmodule

module ALU (
  input  [2:0] ALUop,
  input  [15:0] in1,
  input  [15:0] in2,
  output z,
  output [15:0] result
);

  wire decoder_1_out2;
  wire [15:0] adder_sub_1_result, and_1_out, not_1_out;

  Decoder #(.select(3), .enable("false")) decoder_1 (
    .out2(decoder_1_out2), .sel(ALUop));  // open: out0, out1, out3, out4, out5, out6, out7
  assign not_1_out = ~in1;  // NOT_Gate not_1, 16 bits wide
  assign and_1_out = in1 & in2;  // AND_Gate and_1, 16 bits wide
  adder_sub adder_sub_1 (
    .A(in1), .B(in2), .sub(decoder_1_out2), .result(adder_sub_1_result), .z(z));  // open: unsigned_ovf, signed_ovf
  Multiplexer #(.select(3), .width(16), .enable("false")) multiplexer_1 (
    .in0(adder_sub_1_result), .in1(adder_sub_1_result), .in2(adder_sub_1_result), .in5(and_1_out),
    .in6(not_1_out), .out(result), .sel(ALUop));  // open: in3, in4, in7

  // Other names for the same wires on the sheet: op[2:0] = ALUop
endmodule

module adder_sub (
  input  [15:0] A,
  input  [15:0] B,
  input  sub,
  output unsigned_ovf,
  output signed_ovf,
  output [15:0] result,
  output z
);

  wire bit_adder_1_cout, bit_adder_2_cout, bit_adder_3_cout, bit_adder_4_cout, bit_adder_5_cout,
       bit_adder_6_cout, bit_adder_7_cout, bit_adder_8_cout, bit_adder_9_cout, bit_adder_10_cout,
       bit_adder_11_cout, bit_adder_12_cout, bit_adder_13_cout, bit_adder_14_cout, bit_adder_15_cout;

  bit_adder bit_adder_1 (.Cin(sub), .A(A[0]), .B(B[0]), .subi(sub), .sum(result[0]), .Cout(bit_adder_1_cout));
  bit_adder bit_adder_2 (
    .Cin(bit_adder_15_cout), .A(A[8]), .B(B[8]), .subi(sub), .sum(result[8]), .Cout(bit_adder_2_cout));
  bit_adder bit_adder_3 (
    .Cin(bit_adder_1_cout), .A(A[1]), .B(B[1]), .subi(sub), .sum(result[1]), .Cout(bit_adder_3_cout));
  bit_adder bit_adder_4 (
    .Cin(bit_adder_2_cout), .A(A[9]), .B(B[9]), .subi(sub), .sum(result[9]), .Cout(bit_adder_4_cout));
  bit_adder bit_adder_5 (
    .Cin(bit_adder_3_cout), .A(A[2]), .B(B[2]), .subi(sub), .sum(result[2]), .Cout(bit_adder_5_cout));
  bit_adder bit_adder_6 (
    .Cin(bit_adder_4_cout), .A(A[10]), .B(B[10]), .subi(sub), .sum(result[10]), .Cout(bit_adder_6_cout));
  bit_adder bit_adder_7 (
    .Cin(bit_adder_5_cout), .A(A[3]), .B(B[3]), .subi(sub), .sum(result[3]), .Cout(bit_adder_7_cout));
  bit_adder bit_adder_8 (
    .Cin(bit_adder_6_cout), .A(A[11]), .B(B[11]), .subi(sub), .sum(result[11]), .Cout(bit_adder_8_cout));
  bit_adder bit_adder_9 (
    .Cin(bit_adder_7_cout), .A(A[4]), .B(B[4]), .subi(sub), .sum(result[4]), .Cout(bit_adder_9_cout));
  bit_adder bit_adder_10 (
    .Cin(bit_adder_8_cout), .A(A[12]), .B(B[12]), .subi(sub), .sum(result[12]), .Cout(bit_adder_10_cout));
  bit_adder bit_adder_11 (
    .Cin(bit_adder_9_cout), .A(A[5]), .B(B[5]), .subi(sub), .sum(result[5]), .Cout(bit_adder_11_cout));
  bit_adder bit_adder_12 (
    .Cin(bit_adder_10_cout), .A(A[13]), .B(B[13]), .subi(sub), .sum(result[13]), .Cout(bit_adder_12_cout));
  or or_1 (z, result[0], result[1], result[2], result[3], result[4], result[5], result[6], result[7], result[8], result[9], result[10], result[11], result[12], result[13], result[14], result[15]);
  bit_adder bit_adder_13 (
    .Cin(bit_adder_11_cout), .A(A[6]), .B(B[6]), .subi(sub), .sum(result[6]), .Cout(bit_adder_13_cout));
  bit_adder bit_adder_14 (
    .Cin(bit_adder_12_cout), .A(A[14]), .B(B[14]), .subi(sub), .sum(result[14]), .Cout(bit_adder_14_cout));
  bit_adder bit_adder_15 (
    .Cin(bit_adder_13_cout), .A(A[7]), .B(B[7]), .subi(sub), .sum(result[7]), .Cout(bit_adder_15_cout));
  bit_adder bit_adder_16 (
    .Cin(bit_adder_14_cout), .A(A[15]), .B(B[15]), .subi(sub), .sum(result[15]), .Cout(unsigned_ovf));
  xor xor_1 (signed_ovf, bit_adder_14_cout, unsigned_ovf);

  // Other names for the same wires on the sheet: R0 = result[0]; R1 = result[1]; R2 = result[2]; R3 = result[3];
  //   R4 = result[4]; R5 = result[5]; R6 = result[6]; R7 = result[7]; R8 = result[8]; R9 = result[9];
  //   R10 = result[10]; R11 = result[11]; R12 = result[12]; R13 = result[13]; R14 = result[14]; R15 = result[15];
  //   subi = sub
endmodule

module bit_adder (
  input  Cin,
  input  A,
  input  B,
  input  subi,
  output sum,
  output Cout
);

  wire and_1_out, and_2_out, xor_1_out, xor_2_out;

  and and_1 (and_1_out, xor_1_out, A);
  xor xor_1 (xor_1_out, subi, B);
  or or_1 (Cout, and_1_out, and_2_out);
  xor xor_2 (xor_2_out, A, xor_1_out);
  and and_2 (and_2_out, xor_2_out, Cin);
  xor xor_3 (sum, Cin, xor_2_out);
endmodule

module DRAM (
  input  [15:0] addrIn,
  input  DMwe,
  input  clk,
  input  [15:0] dataIn,
  output [15:0] dataOut
);

  wire memory_latch_1_oe_latched, memory_latch_1_we_latched, not_1_out;
  wire [15:0] memory_latch_1_address_latched, memory_latch_1_data_in_latched;

  not not_1 (not_1_out, clk);
  memory_latch memory_latch_1 (
    .address(addrIn), .WE(DMwe), .clk(not_1_out), .data_in(dataIn),
    .address_latched(memory_latch_1_address_latched), .WE_latched(memory_latch_1_we_latched),
    .OE_latched(memory_latch_1_oe_latched), .data_in_latched(memory_latch_1_data_in_latched));
  RAM #(.addrWidth(16), .dataWidth(16), .trigger("high"), .databus("bibus")) ram_1 (
    .addr(memory_latch_1_address_latched), .we(memory_latch_1_we_latched), .oe(memory_latch_1_oe_latched),
    .din(memory_latch_1_data_in_latched), .dout(dataOut));
endmodule

module memory_latch (
  input  [15:0] address,
  input  WE,
  input  clk,
  input  [15:0] data_in,
  output [15:0] address_latched,
  output WE_latched,
  output OE_latched,
  output [15:0] data_in_latched
);

  wire DMwe_latch_q;
  wire [15:0] addr_latch_q;

  Register #(.width(16), .trigger("falling")) addr_latch (
    .D(address), .en(WE), .clk(clk), .Q(addr_latch_q));  // open: clr
  D_Flip_Flop #(.trigger("falling")) DMwe_latch (.D(WE), .clk(clk), .Q(DMwe_latch_q));  // open: Qn, preset, reset
  Register #(.width(16), .trigger("falling")) data_to_be_written (
    .D(data_in), .en(WE), .clk(clk), .Q(data_in_latched));  // open: clr
  Multiplexer #(.width(16), .enable("false")) multiplexer_1 (
    .in0(address), .in1(addr_latch_q), .out(address_latched), .sel(DMwe_latch_q));
  and and_1 (WE_latched, clk, DMwe_latch_q);
  not not_1 (OE_latched, WE_latched);
endmodule
